# Fritzing sketch Light-Control-Schematic (saved by Fritzing 0.9.3b)
breadboards: 1

parts:
  IC1 = IC, DIP package, 8 pins [chip_label=IC]
  IC2 = IC, DIP package, 8 pins [chip_label=IC]
  IC3 = IC, DIP package, 8 pins [chip_label=IC]
  Part1 = Arduino Board Ethernet
  LED1 = RGB LED (com. anode, rbg) [package="5 mm [THT]"]
  BAT1 = Battery Holders [package=lipo-1100mAh]

nets:
  N1: IC1.pin1, Part1.D10_PWM/SS
  N2: IC1.pin4, IC2.pin4, IC3.pin4
  N3: IC1.pin5, LED1.red_cathode
  N4: IC1.pin6, IC2.pin6, IC3.pin6, Part1.D11/MOSI
  N5: IC1.pin7, IC2.pin7, IC3.pin7, BAT1.+
  N6: IC1.pin8, IC2.pin8, IC3.pin8
  N7: IC2.pin1, Part1.D9_PWM
  N8: IC2.pin5, LED1.blue_cathode
  N9: IC3.pin1, Part1.D8
  N10: IC3.pin5, LED1.green_cathode
